# Fritzing sketch Sensors (saved by Fritzing 0.9.3b)
breadboards: 1

parts:
  R1 = Resistor [tolerance=±5% resistance=10k package=THT]
  Part1 = Arduino Uno (Rev3)
  T1 = LM35 Temperature Sensor [package="TO92 [THT]"]
  T2 = LM35 Temperature Sensor [package="TO92 [THT]"]
  R2 = Resistor [tolerance=±5% resistance=10k package=THT]
  J1 = female pin header, 3 pins [form="♀ (female)"]

nets:
  GND: R1.Pin_0, Part1.GND, T1.GND, T2.GND, R2.Pin_0, J1.pin3
  N1: R1.Pin_1, Part1.A1, T1.Vout
  N2: Part1.A0, J1.pin1
  N3: Part1.A5/SCL, T2.Vout, R2.Pin_1
  N4: Part1.5V, T1.+Vs, T2.+Vs, J1.pin2
